// Logisim project Circuit.circ as structural Verilog: 6 circuits, main circuit main
module main (
  input  RESET
);

  wire clock_1_out, decodeur_instruction_1_isjmp, decodeur_instruction_1_isload,
       decodeur_instruction_1_regwrite;
  wire [1:0] controle_saut_1_nextpcselect;
  wire [2:0] decodeur_instruction_1_ctrual;
  wire [3:0] selection_registre_1_p2, selection_registre_1_p4, selection_registre_1_p6, ual_1_flags;
  wire [7:0] adder_1_out, adder_2_out, banc_de_registre_1_rs_2, banc_de_registre_1_rt_2, bit_extender_1_out,
       multiplexer_1_out, multiplexer_2_out, PC_q, ual_1_rd;
  wire [15:0] ram_1_data;

  Register PC (.D(multiplexer_2_out), .en(1'b1), .Q(PC_q), .clk(clock_1_out), .clr(RESET));
  Clock clock_1 (.out(clock_1_out));
  Adder adder_1 (.a(PC_q), .b(8'h1), .out(adder_1_out));  // open: cin, cout
  RAM #(.dataWidth(16)) ram_1 (.addr(PC_q), .data(ram_1_data), .clk(clock_1_out));  // open: sel, ld, clr
  DECODEUR_INSTRUCTION decodeur_instruction_1 (
    .Opcode(ram_1_data[15:12]), .isJMP(decodeur_instruction_1_isjmp),
    .regWrite(decodeur_instruction_1_regwrite), .isLoad(decodeur_instruction_1_isload),
    .ctrUAL(decodeur_instruction_1_ctrual));
  // SELECTION_REGISTRE selection_registre_1: pin names not known; wires that end beside it: decodeur_instruction_1_isjmp, selection_registre_1_p2, ram_1_data[11:8], selection_registre_1_p4, ram_1_data[7:4], selection_registre_1_p6, ram_1_data[3:0]
  Multiplexer #(.width(8)) multiplexer_1 (
    .in0(ram_1_data[7:0]), .in1(ual_1_rd), .out(multiplexer_1_out), .sel(decodeur_instruction_1_isload));  // open: en
  assign bit_extender_1_out = {{4{1'b0}}, ram_1_data[3:0]};  // Bit_Extender bit_extender_1
  BANC_DE_REGISTRE banc_de_registre_1 (
    .valIn(multiplexer_1_out), .regWrite(decodeur_instruction_1_regwrite), .rd(selection_registre_1_p2),
    .Horloge(clock_1_out), .Reset(RESET), .Rs_2(banc_de_registre_1_rs_2), .rs(selection_registre_1_p4),
    .Rt_2(banc_de_registre_1_rt_2), .rt(selection_registre_1_p6));
  Adder adder_2 (.a(adder_1_out), .b(bit_extender_1_out), .out(adder_2_out));  // open: cin, cout
  UAL ual_1 (
    .Rs(banc_de_registre_1_rs_2), .Rt(banc_de_registre_1_rt_2), .Rd(ual_1_rd), .flags(ual_1_flags),
    .ctrUAL(decodeur_instruction_1_ctrual));
  Multiplexer #(.select(2), .width(8)) multiplexer_2 (
    .in0(adder_1_out), .in1({8{1'b1}}), .in3(adder_2_out), .out(multiplexer_2_out),
    .sel(controle_saut_1_nextpcselect));  // open: in2, en
  CONTROLE_SAUT controle_saut_1 (
    .flags(ual_1_flags), .opCode(ram_1_data[15:12]), .nextPCselect(controle_saut_1_nextpcselect));
endmodule

module UAL (
  input  [7:0] Rs,
  input  [2:0] ctrUAL,
  input  [7:0] Rt,
  output [3:0] flags,
  output [7:0] Rd
);

  wire adder_1_cout, and_2_out, and_3_out, subtractor_1_bout;
  wire [7:0] adder_1_out, and_1_out, not_1_out, or_1_out, shifter_1_out, shifter_2_out, subtractor_1_out;

  assign not_1_out = ~Rs;  // NOT_Gate not_1, 8 bits wide
  Multiplexer #(.select(3)) multiplexer_1 (
    .in0(adder_1_cout), .in1(subtractor_1_bout), .in2(1'b0), .in3(1'b0), .in4(1'b0), .in5(1'b0), .in6(1'b0),
    .in7(1'b0), .out(flags[3]), .sel(ctrUAL));  // open: en
  Adder adder_1 (.a(Rs), .b(Rt), .out(adder_1_out), .cout(adder_1_cout));  // open: cin
  Subtractor subtractor_1 (.a(Rs), .b(Rt), .out(subtractor_1_out), .bout(subtractor_1_bout));  // open: bin
  assign or_1_out = Rs | Rt;  // OR_Gate or_1, 8 bits wide
  assign and_1_out = Rs & Rt;  // AND_Gate and_1, 8 bits wide
  Shifter shifter_1 (.in(Rs), .\dist (Rt[2:0]), .out(shifter_1_out));
  Shifter #(.shift("lr")) shifter_2 (.in(Rs), .\dist (Rt[2:0]), .out(shifter_2_out));
  Multiplexer #(.select(3), .width(8)) multiplexer_2 (
    .in0(adder_1_out), .in1(subtractor_1_out), .in2(or_1_out), .in3(and_1_out), .in4(not_1_out),
    .in5(shifter_1_out), .in6(shifter_2_out), .in7({8{1'b0}}), .out({flags[1], Rd[6:0]}), .sel(ctrUAL));  // open: en
  nor nor_1 (flags[2], flags[1], Rd[6], Rd[5], Rd[4], Rd[3], Rd[2], Rd[1], Rd[0]);
  and and_2 (and_2_out, Rs[7], Rt[7], ~flags[1]);  // AND_Gate
  and and_3 (and_3_out, ~Rs[7], ~Rt[7], flags[1]);  // AND_Gate
  or or_2 (flags[0], and_2_out, and_3_out);

  assign Rd[7] = flags[1];

  // Other names for the same wires on the sheet: Overflow = flags[0]; RdO = flags[1]; RsO = Rs[7]; RtO = Rt[7]
endmodule

// DECODEUR \nD'INSCRUCTION
module DECODEUR_INSTRUCTION (
  input  [3:0] Opcode,
  output isJMP,
  output regWrite,
  output isLoad,
  output [2:0] ctrUAL
);

  wire or_1_out;

  not not_1 (regWrite, Opcode[0]);
  and and_1 (isLoad, ~Opcode[0], Opcode[1], Opcode[2], Opcode[3]);  // AND_Gate
  or or_1 (or_1_out, Opcode[2], Opcode[1], Opcode[0]);
  and and_2 (isJMP, Opcode[3], or_1_out);

  assign ctrUAL = Opcode[2:0];

  // Other names for the same wires on the sheet: A = Opcode[0]; B = Opcode[1]; C = Opcode[2]; D = Opcode[3]

  // Notes on the sheet:
  //   ctrUAL pas sur du tout a revoir
endmodule

// CONTROLE \nDE SAUT
module CONTROLE_SAUT (
  input  [3:0] flags,
  input  [3:0] opCode,
  output [1:0] nextPCselect
);
endmodule

// SELECTION\n REGISTRES
module SELECTION_REGISTRE (
  input  [3:0] rd_rs,
  input  [3:0] rs_rt,
  input  [3:0] rt,
  input  isJMP,
  output [3:0] rd,
  output [3:0] rs,
  output [3:0] rt_2
);

  Multiplexer #(.width(4)) multiplexer_1 (.in0(rs_rt), .in1(rd_rs), .out(rs), .sel(isJMP));  // open: en
  Multiplexer #(.width(4)) multiplexer_2 (.in0(rt), .in1(rs_rt), .out(rt_2), .sel(isJMP));  // open: en

  assign rd = rd_rs;
endmodule

// BANC DE REGISTRES
module BANC_DE_REGISTRE (
  input  [7:0] valIn,
  input  regWrite,
  input  [3:0] rd,
  input  [3:0] rs,
  input  Horloge,
  input  [3:0] rt,
  input  Reset,
  output [7:0] Rs_2,
  output [7:0] Rt_2
);

  wire demultiplexer_2_out0, demultiplexer_2_out1, demultiplexer_2_out2, demultiplexer_2_out3,
       demultiplexer_2_out4, demultiplexer_2_out5, demultiplexer_2_out6, demultiplexer_2_out7,
       demultiplexer_2_out8, demultiplexer_2_out9, demultiplexer_2_out10, demultiplexer_2_out11,
       demultiplexer_2_out12, demultiplexer_2_out13, demultiplexer_2_out14, demultiplexer_2_out15;
  wire [7:0] demultiplexer_1_out0, demultiplexer_1_out1, demultiplexer_1_out2, demultiplexer_1_out3,
       demultiplexer_1_out4, demultiplexer_1_out5, demultiplexer_1_out6, demultiplexer_1_out7,
       demultiplexer_1_out8, demultiplexer_1_out9, demultiplexer_1_out10, demultiplexer_1_out11,
       demultiplexer_1_out12, demultiplexer_1_out13, demultiplexer_1_out14, demultiplexer_1_out15, R1, R2,
       R3, R4, R5, R6, R7, R8, R9, R10, R11, R12, R13, R14, R15, R16;

  Demultiplexer #(.select(4), .width(8)) demultiplexer_1 (
    .out0(demultiplexer_1_out0), .out1(demultiplexer_1_out1), .out2(demultiplexer_1_out2),
    .out3(demultiplexer_1_out3), .out4(demultiplexer_1_out4), .out5(demultiplexer_1_out5),
    .out6(demultiplexer_1_out6), .out7(demultiplexer_1_out7), .out8(demultiplexer_1_out8),
    .out9(demultiplexer_1_out9), .out10(demultiplexer_1_out10), .out11(demultiplexer_1_out11),
    .out12(demultiplexer_1_out12), .out13(demultiplexer_1_out13), .out14(demultiplexer_1_out14),
    .out15(demultiplexer_1_out15), .in(valIn), .sel(rd), .en(regWrite));
  Demultiplexer #(.select(4)) demultiplexer_2 (
    .out0(demultiplexer_2_out0), .out1(demultiplexer_2_out1), .out2(demultiplexer_2_out2),
    .out3(demultiplexer_2_out3), .out4(demultiplexer_2_out4), .out5(demultiplexer_2_out5),
    .out6(demultiplexer_2_out6), .out7(demultiplexer_2_out7), .out8(demultiplexer_2_out8),
    .out9(demultiplexer_2_out9), .out10(demultiplexer_2_out10), .out11(demultiplexer_2_out11),
    .out12(demultiplexer_2_out12), .out13(demultiplexer_2_out13), .out14(demultiplexer_2_out14),
    .out15(demultiplexer_2_out15), .in(Horloge), .sel(rd), .en(regWrite));
  Register register_1 (.D(demultiplexer_1_out0), .Q(R1), .clk(demultiplexer_2_out0), .clr(Reset));  // open: en
  Register register_2 (.D(demultiplexer_1_out4), .Q(R5), .clk(demultiplexer_2_out4), .clr(Reset));  // open: en
  Register register_3 (.D(demultiplexer_1_out8), .Q(R9), .clk(demultiplexer_2_out8), .clr(Reset));  // open: en
  Register register_4 (.D(demultiplexer_1_out12), .Q(R13), .clk(demultiplexer_2_out12), .clr(Reset));  // open: en
  Register register_5 (.D(demultiplexer_1_out1), .Q(R2), .clk(demultiplexer_2_out1), .clr(Reset));  // open: en
  Register register_6 (.D(demultiplexer_1_out5), .Q(R6), .clk(demultiplexer_2_out5), .clr(Reset));  // open: en
  Register register_7 (.D(demultiplexer_1_out9), .Q(R10), .clk(demultiplexer_2_out9), .clr(Reset));  // open: en
  Register register_8 (.D(demultiplexer_1_out13), .Q(R14), .clk(demultiplexer_2_out13), .clr(Reset));  // open: en
  Register register_9 (.D(demultiplexer_1_out2), .Q(R3), .clk(demultiplexer_2_out2), .clr(Reset));  // open: en
  Register register_10 (.D(demultiplexer_1_out6), .Q(R7), .clk(demultiplexer_2_out6), .clr(Reset));  // open: en
  Register register_11 (.D(demultiplexer_1_out10), .Q(R11), .clk(demultiplexer_2_out10), .clr(Reset));  // open: en
  Register register_12 (.D(demultiplexer_1_out14), .Q(R15), .clk(demultiplexer_2_out14), .clr(Reset));  // open: en
  Register register_13 (.D(demultiplexer_1_out3), .Q(R4), .clk(demultiplexer_2_out3), .clr(Reset));  // open: en
  Register register_14 (.D(demultiplexer_1_out7), .Q(R8), .clk(demultiplexer_2_out7), .clr(Reset));  // open: en
  Register register_15 (.D(demultiplexer_1_out11), .Q(R12), .clk(demultiplexer_2_out11), .clr(Reset));  // open: en
  Register register_16 (.D(demultiplexer_1_out15), .Q(R16), .clk(demultiplexer_2_out15), .clr(Reset));  // open: en
  Multiplexer #(.select(4), .width(8)) multiplexer_1 (
    .in0(R1), .in1(R2), .in2(R3), .in3(R4), .in4(R5), .in5(R6), .in6(R7), .in7(R8), .in8(R9), .in9(R10),
    .in10(R11), .in11(R12), .in12(R13), .in13(R14), .in14(R15), .in15(R16), .out(Rs_2), .sel(rs));  // open: en
  Multiplexer #(.select(4), .width(8)) multiplexer_2 (
    .in0(R1), .in1(R2), .in2(R3), .in3(R4), .in4(R5), .in5(R6), .in6(R7), .in7(R8), .in8(R9), .in9(R10),
    .in10(R11), .in11(R12), .in12(R13), .in13(R14), .in14(R15), .in15(R16), .out(Rt_2), .sel(rt));  // open: en
endmodule
